# Fritzing sketch Mark1 (saved by Fritzing 0.9.3b)
breadboards: 1

parts:
  Part1 = Arduino Uno (Rev3)
  IC1 = L293D [package=THT]
  M2 = DC Motor
  M3 = DC Motor
  hc-sr1 = hc-sr04
  BAT1 = BC9VPC [package=bc9vpc]
  IR1 = TSOP312.., 314.. [package=THT]
  BAT2 = BC9VPC [package=bc9vpc]
  J1 = Basic Servo
  Part2 = MicroSD Card Module  # not connected

nets:
  N1: Part1.A0, IC1.In_4
  N2: Part1.D8, IC1.In_2
  N3: Part1.D9_PWM, J1.pulse
  N4: Part1.D10_PWM/SS, IR1.Data
  GND: Part1.GND, IC1.0V, IC1.+Vmotor, hc-sr1.GND, BAT1.V-, IR1.GND, BAT2.V-
  N5: Part1.D2, IC1.In_1
  N6: Part1.D3_PWM, IC1.Enable_1
  N7: Part1.D4, IC1.In_3
  N8: Part1.D5_PWM, IC1.Enable_2
  N9: Part1.D6_PWM, hc-sr1.Echo
  N10: Part1.D7, hc-sr1.Trig
  5V: Part1.5V, hc-sr1.VCC, IR1.Vs
  N11: Part1.VIN, BAT1.V+
  N12: IC1.Out_1_(_Controlled_by_Enable_1_), M3.pin_2
  N13: IC1.Out_2_(_Controlled_by_Enable_1_), M3.pin_1
  N14: IC1.Out_3_(_Controlled_by_Enable_2_), M2.pin_2
  N15: IC1.Out_4_(_Controlled_by_Enable_2_), M2.pin_1
